# Fritzing sketch recoboard_quarter (saved by Fritzing 0.9.4)
circuit board: 8.46667cm x 5.64444cm
breadboards: 2

parts:
  Raspberry_Pi_1 = Raspberry Pi 3 [part_number=RPI-3-V1.2]  # not connected
  U1 = MCP23017 [package=dil28-3]
  Part1 = RFID-RC522-v2
  Part2 = RFID-RC522-v2
  Part3 = RFID-RC522-v2
  Part4 = RFID-RC522-v2
  Part6 = RFID-RC522-v2
  Part7 = RFID-RC522-v2
  Part8 = RFID-RC522-v2
  Part9 = RFID-RC522-v2
  Part10 = RFID-RC522-v2
  Part11 = RFID-RC522-v2
  Part12 = RFID-RC522-v2
  Part13 = RFID-RC522-v2
  Part14 = RFID-RC522-v2
  Part15 = RFID-RC522-v2
  Part16 = RFID-RC522-v2
  Part4_2 = RFID-RC522-v2
  M1 = RioRand LM2596  # not connected
  Part17 = RFID-RC522-v2  # not connected

nets:
  N1: U1.GPA0, U1.GPA1, U1.GPA5, U1.GPA6, U1.GPA7, Part10.SDA, Part13.SDA, Part14.SDA, Part16.SDA, Part4_2.SDA
  N2: U1.GPA2, Part11.SDA
  N3: U1.GPA3, Part15.SDA
  N4: U1.GPA4, Part12.SDA
  N5: U1.GPB0, Part9.SDA
  N6: U1.GPB1, Part4.SDA
  N7: U1.GPB2, Part8.SDA
  N8: U1.GPB3, Part3.SDA
  N9: U1.GPB4, Part7.SDA
  N10: U1.GPB5, Part2.SDA
  N11: U1.GPB6, Part6.SDA
  N12: U1.GPB7, Part1.SDA
  N13: Part1.SCK, Part2.SCK, Part3.SCK, Part4.SCK, Part6.SCK, Part7.SCK, Part8.SCK, Part9.SCK, Part10.SCK, Part11.SCK, Part12.SCK, Part13.SCK, Part14.SCK, Part15.SCK, Part16.SCK, Part4_2.SCK
  N14: Part1.MOSI, Part2.MOSI, Part3.MOSI, Part4.MOSI, Part6.MOSI, Part7.MOSI, Part8.MOSI, Part9.MOSI, Part10.MOSI, Part11.MOSI, Part12.MOSI, Part13.MOSI, Part14.MOSI, Part15.MOSI, Part16.MOSI, Part4_2.MOSI
  N15: Part1.MISO, Part2.MISO, Part3.MISO, Part4.MISO, Part6.MISO, Part7.MISO, Part8.MISO, Part9.MISO, Part10.MISO, Part11.MISO, Part12.MISO, Part13.MISO, Part14.MISO, Part15.MISO, Part16.MISO, Part4_2.MISO
  GND: Part1.GND, Part2.GND, Part3.GND, Part4.GND, Part6.GND, Part7.GND, Part8.GND, Part9.GND, Part10.GND, Part11.GND, Part12.GND, Part13.GND, Part14.GND, Part15.GND, Part16.GND, Part4_2.GND
  N16: Part1.RST, Part2.RST, Part3.RST, Part4.RST, Part6.RST, Part7.RST, Part8.RST, Part9.RST, Part10.RST, Part11.RST, Part12.RST, Part13.RST, Part14.RST, Part15.RST, Part16.RST, Part4_2.RST
  3.3V: Part1.3.3V, Part2.3.3V, Part3.3.3V, Part4.3.3V, Part6.3.3V, Part7.3.3V, Part8.3.3V, Part9.3.3V, Part10.3.3V, Part11.3.3V, Part12.3.3V, Part13.3.3V, Part14.3.3V, Part15.3.3V, Part16.3.3V, Part4_2.3.3V

custom parts:
  MCP23017: 16 bit I/O chip controlled via I2C
  RFID-RC522-v2: A simple China made RFID-RC522 Reader; do check the pin labels, as this is a MFRC522 based clone.
